// Logisim project CINHOS.circ as structural Verilog: 12 circuits, main circuit main
module main (
  input  D,
  input  [3:0] B,
  input  [3:0] A,
  input  [2:0] Controle,
  output out_5,
  output [3:0] out_6
);

  wire dec_3x8_1_a, dec_3x8_1_b, dec_3x8_1_c, dec_3x8_1_d, dec_3x8_1_e, not_2_out;
  wire [3:0] add_4_1_out_4, buffer_5_out_3, not_1_out_2, or_1_s, rot_d_1_out_3, rot_e_1_abcd_2;

  Dec__3x8 dec_3x8_1 (
    .Controle(Controle), .a(dec_3x8_1_a), .b(dec_3x8_1_b), .c(dec_3x8_1_c), .d(dec_3x8_1_d), .e(dec_3x8_1_e));  // open: f, g, h
  Buffer buffer_1 (.B(B), .C(dec_3x8_1_a), .out_3(out_6));
  ADD_4 add_4_1 (.out_3(out_5), .A(A), .B(B), .out_4(add_4_1_out_4));
  Buffer buffer_2 (.B(add_4_1_out_4), .C(dec_3x8_1_b), .out_3(out_6));
  OR or_1 (.B(A), .A(B), .S(or_1_s));
  Buffer buffer_3 (.B(or_1_s), .C(dec_3x8_1_c), .out_3(out_6));
  NOT not_1 (.B(B), .out_2(not_1_out_2));
  Buffer buffer_4 (.B(not_1_out_2), .C(dec_3x8_1_d), .out_3(out_6));
  ROT_E rot_e_1 (.ABCD_2(rot_e_1_abcd_2), .abcd(A), .XY(B[1:0]));
  ROT_D rot_d_1 (.out_3(rot_d_1_out_3), .ABCD(A), .XY(B[1:0]));
  Buffer buffer_5 (.B(rot_e_1_abcd_2), .C(not_2_out), .out_3(buffer_5_out_3));
  not not_2 (not_2_out, D);
  Buffer buffer_6 (.B(rot_d_1_out_3), .C(D), .out_3(buffer_5_out_3));
  Buffer buffer_7 (.B(buffer_5_out_3), .C(dec_3x8_1_e), .out_3(out_6));
endmodule

module ADD_1 (
  input  A,
  input  B,
  input  Vem_1,
  output S,
  output Vem_1_2
);

  wire and_1_out, and_2_out, and_3_out, and_4_out, and_5_out, and_6_out, and_7_out, not_1_out, not_2_out,
       not_3_out, not_4_out, not_5_out, not_6_out;

  not not_1 (not_1_out, A);
  not not_2 (not_2_out, B);
  not not_3 (not_3_out, A);
  not not_4 (not_4_out, Vem_1);
  not not_5 (not_5_out, B);
  not not_6 (not_6_out, Vem_1);
  and and_1 (and_1_out, B, Vem_1);
  and and_2 (and_2_out, A, Vem_1);
  and and_3 (and_3_out, A, B);
  and and_4 (and_4_out, not_1_out, not_2_out, Vem_1);
  and and_5 (and_5_out, not_3_out, B, not_4_out);
  and and_6 (and_6_out, A, not_5_out, not_6_out);
  and and_7 (and_7_out, A, B, Vem_1);
  or or_1 (Vem_1_2, and_1_out, and_2_out, and_3_out);
  ExactlyOne xor_1 (.out(S), .in0(and_4_out), .in1(and_5_out), .in2(and_6_out), .in3(and_7_out));
endmodule

module ADD_4 (
  input  [3:0] B,
  input  [3:0] A,
  output out_3,
  output [3:0] out_4
);

  wire add_1_2_vem_1_2, add_1_3_vem_1_2, add_1_4_vem_1_2;

  // Probe on A
  ADD_1 add_1_1 (.A(A[3]), .B(B[3]), .Vem_1(add_1_2_vem_1_2), .S(out_4[3]), .Vem_1_2(out_3));
  ADD_1 add_1_2 (.A(A[2]), .B(B[2]), .Vem_1(add_1_3_vem_1_2), .S(out_4[2]), .Vem_1_2(add_1_2_vem_1_2));
  ADD_1 add_1_3 (.A(A[1]), .B(B[1]), .Vem_1(add_1_4_vem_1_2), .S(out_4[1]), .Vem_1_2(add_1_3_vem_1_2));
  // Probe on out_4
  ADD_1 add_1_4 (.A(A[0]), .B(B[0]), .Vem_1(1'b0), .S(out_4[0]), .Vem_1_2(add_1_4_vem_1_2));
  // Probe on B
endmodule

module Dec__3x8 (
  input  [2:0] Controle,
  output a,
  output b,
  output c,
  output d,
  output e,
  output f,
  output g,
  output h
);

  wire not_1_out, not_2_out, not_3_out, not_4_out, not_5_out, not_6_out, not_7_out, not_8_out, not_9_out,
       not_10_out, not_11_out, not_12_out;

  not not_1 (not_1_out, Controle[2]);
  not not_2 (not_2_out, Controle[1]);
  not not_3 (not_3_out, Controle[0]);
  not not_4 (not_4_out, Controle[2]);
  not not_5 (not_5_out, Controle[1]);
  not not_6 (not_6_out, Controle[2]);
  not not_7 (not_7_out, Controle[0]);
  not not_8 (not_8_out, Controle[2]);
  not not_9 (not_9_out, Controle[1]);
  not not_10 (not_10_out, Controle[0]);
  not not_11 (not_11_out, Controle[1]);
  not not_12 (not_12_out, Controle[0]);
  and and_1 (h, Controle[2], Controle[1], Controle[0]);
  and and_2 (a, not_1_out, not_2_out, not_3_out);
  and and_3 (b, not_4_out, not_5_out, Controle[0]);
  and and_4 (c, not_6_out, Controle[1], not_7_out);
  and and_5 (d, not_8_out, Controle[1], Controle[0]);
  and and_6 (e, Controle[2], not_9_out, not_10_out);
  and and_7 (f, Controle[2], not_11_out, Controle[0]);
  and and_8 (g, Controle[2], Controle[1], not_12_out);
endmodule

module OR (
  input  [3:0] B,
  input  [3:0] A,
  output [3:0] S
);

  or or_1 (S[3], A[3], B[3]);
  or or_2 (S[2], A[2], B[2]);
  or or_3 (S[1], A[1], B[1]);
  or or_4 (S[0], A[0], B[0]);
endmodule

module NOT (
  input  [3:0] B,
  output [3:0] out_2
);

  not not_1 (out_2[3], B[3]);
  not not_2 (out_2[2], B[2]);
  not not_3 (out_2[1], B[1]);
  not not_4 (out_2[0], B[0]);
endmodule

module Buffer (
  input  [3:0] B,
  input  C,
  output [3:0] out_3
);

  assign out_3[2] = C ? B[2] : 1'bz;  // Controlled_Buffer controlled_buffer_1
  assign out_3[3] = C ? B[3] : 1'bz;  // Controlled_Buffer controlled_buffer_2
  assign out_3[1] = C ? B[1] : 1'bz;  // Controlled_Buffer controlled_buffer_3
  assign out_3[0] = C ? B[0] : 1'bz;  // Controlled_Buffer controlled_buffer_4
endmodule

module OR_4 (
  input  [3:0] B,
  input  [3:0] A,
  output [3:0] S
);

  or or_1 (S[3], A[3], B[3]);
  or or_2 (S[2], A[2], B[2]);
  or or_3 (S[1], A[1], B[1]);
  or or_4 (S[0], A[0], B[0]);
endmodule

module ROT_D (
  input  [3:0] ABCD,
  input  [1:0] XY,
  output [3:0] out_3
);

  wire and_1_out, and_2_out, and_3_out, and_4_out, and_5_out, and_6_out, and_7_out, and_8_out, and_9_out;

  and and_1 (and_1_out, ~XY[1], ~XY[0], ABCD[0]);  // AND_Gate
  and and_2 (and_2_out, ~XY[1], XY[0], ABCD[1]);  // AND_Gate
  and and_3 (and_3_out, XY[1], ~XY[0], ABCD[2]);  // AND_Gate
  and and_4 (and_4_out, XY[1], XY[0], ABCD[3]);
  and and_5 (and_5_out, ~XY[1], ~XY[0], ABCD[1]);  // AND_Gate
  and and_6 (and_6_out, ~XY[1], XY[0], ABCD[2]);  // AND_Gate
  and and_7 (and_7_out, XY[1], ~XY[0], ABCD[3]);  // AND_Gate
  and and_8 (and_8_out, ~XY[1], ~XY[0], ABCD[2]);  // AND_Gate
  and and_9 (and_9_out, ~XY[1], XY[0], ABCD[3]);  // AND_Gate
  and and_10 (out_3[3], ~XY[1], ~XY[0], ABCD[3]);  // AND_Gate
  or or_1 (out_3[0], and_1_out, and_2_out, and_3_out, and_4_out);
  or or_2 (out_3[1], and_5_out, and_6_out, and_7_out);
  or or_3 (out_3[2], and_8_out, and_9_out);
endmodule

module SUB_1 (
  input  A,
  input  B,
  input  VEM_1,
  output S,
  output VAI_1
);

  wire and_1_out, and_2_out, and_3_out, and_4_out, and_5_out, and_6_out, and_7_out, not_1_out, not_2_out,
       not_3_out, not_4_out, not_5_out, not_6_out, not_7_out, not_8_out;

  not not_1 (not_1_out, A);
  not not_2 (not_2_out, B);
  not not_3 (not_3_out, A);
  not not_4 (not_4_out, VEM_1);
  not not_5 (not_5_out, B);
  not not_6 (not_6_out, VEM_1);
  not not_7 (not_7_out, A);
  not not_8 (not_8_out, A);
  and and_1 (and_1_out, not_1_out, not_2_out, VEM_1);
  and and_2 (and_2_out, not_3_out, B, not_4_out);
  and and_3 (and_3_out, A, not_5_out, not_6_out);
  and and_4 (and_4_out, A, B, VEM_1);
  and and_5 (and_5_out, not_7_out, VEM_1);
  and and_6 (and_6_out, not_8_out, B);
  and and_7 (and_7_out, B, VEM_1);
  or or_1 (S, and_1_out, and_2_out, and_3_out, and_4_out);
  or or_2 (VAI_1, and_5_out, and_6_out, and_7_out);
endmodule

// A
module SUB_4 (
  input  [3:0] B,
  input  [3:0] A,
  output out_3,
  output [3:0] out_4
);

  wire sub_1_2_vai_1, sub_1_3_vai_1, sub_1_4_vai_1;

  // Probe on A
  SUB_1 sub_1_1 (.A(A[3]), .B(B[3]), .VEM_1(sub_1_2_vai_1), .S(out_4[3]), .VAI_1(out_3));
  SUB_1 sub_1_2 (.A(A[2]), .B(B[2]), .VEM_1(sub_1_3_vai_1), .S(out_4[2]), .VAI_1(sub_1_2_vai_1));
  SUB_1 sub_1_3 (.A(A[1]), .B(B[1]), .VEM_1(sub_1_4_vai_1), .S(out_4[1]), .VAI_1(sub_1_3_vai_1));
  // Probe on out_4
  SUB_1 sub_1_4 (.A(A[0]), .B(B[0]), .VEM_1(1'b0), .S(out_4[0]), .VAI_1(sub_1_4_vai_1));
  // Probe on B
endmodule

module ROT_E (
  input  [3:0] abcd,
  input  [1:0] XY,
  output [3:0] ABCD_2
);

  wire and_1_out, and_2_out, and_3_out, and_4_out, and_5_out, and_6_out, and_7_out, and_8_out, and_9_out;

  and and_1 (and_1_out, ~XY[1], ~XY[0], abcd[3]);  // AND_Gate
  and and_2 (and_2_out, ~XY[1], XY[0], abcd[2]);  // AND_Gate
  and and_3 (and_3_out, XY[1], ~XY[0], abcd[1]);  // AND_Gate
  and and_4 (and_4_out, XY[1], XY[0], abcd[0]);
  and and_5 (and_5_out, ~XY[1], ~XY[0], abcd[2]);  // AND_Gate
  and and_6 (and_6_out, ~XY[1], XY[0], abcd[1]);  // AND_Gate
  and and_7 (and_7_out, XY[1], ~XY[0], abcd[0]);  // AND_Gate
  and and_8 (and_8_out, ~XY[1], ~XY[0], abcd[1]);  // AND_Gate
  and and_9 (and_9_out, ~XY[1], XY[0], abcd[0]);  // AND_Gate
  and and_10 (ABCD_2[0], ~XY[1], ~XY[0], abcd[0]);  // AND_Gate
  or or_1 (ABCD_2[3], and_1_out, and_2_out, and_3_out, and_4_out);
  or or_2 (ABCD_2[2], and_5_out, and_6_out, and_7_out);
  or or_3 (ABCD_2[1], and_8_out, and_9_out);
endmodule
