// Logisim project ULA.circ as structural Verilog: 17 circuits, main circuit ULA
module MAIN (
  input  [3:0] in_1,
  input  R_W_0,
  output out_3,
  output out_4
);

  wire clock_1_out, clock_2_out, clock_3_out, not_1_out;
  wire [3:0] mux_1_s, ram_1_data, ula_1_s, undriven;
  wire [7:0] ir_1_q, rom_1_data;

  Clock clock_1 (.out(clock_1_out));
  Clock clock_2 (.out(clock_2_out));
  // Probe on rom_1_data
  ROM #(.addrWidth(4)) rom_1 (.addr(in_1), .data(rom_1_data));  // open: sel
  IR ir_1 (.Clock(clock_1_out), .Q(ir_1_q), .E(rom_1_data));
  // Probe on ir_1_q
  Mux mux_1 (.Controle(ir_1_q[4]), .A(ir_1_q[3:0]), .b(ram_1_data), .S(mux_1_s));
  // Probe on undriven
  ULA ula_1 (
    .B(mux_1_s), .A(undriven), .Controle(ir_1_q[7:5]), .S(ula_1_s), .D(ir_1_q[4]), .out_5(out_3), .Zero(out_4));
  // Probe on ula_1_s
  AC ac_1 (.in_1(clock_2_out), .Q(ula_1_s), .D(undriven));
  Clock clock_3 (.out(clock_3_out));
  // Probe on mux_1_s
  RAM #(.addrWidth(4), .dataWidth(4)) ram_1 (
    .addr(ir_1_q[3:0]), .data(ram_1_data), .clk(clock_3_out), .ld(R_W_0));  // open: sel, clr
  not not_1 (not_1_out, R_W_0);
  Buffer buffer_1 (.B(undriven), .C(not_1_out), .out_3(ram_1_data));
endmodule

module ULA (
  input  D,
  input  [3:0] B,
  input  [3:0] A,
  input  [2:0] Controle,
  output out_5,
  output [3:0] S,
  output Zero
);

  wire add_4_1_out_3, and_1_out, and_2_out, dec_3x8_1_a, dec_3x8_1_b, dec_3x8_1_c, dec_3x8_1_d, dec_3x8_1_e,
       dec_3x8_1_f, dec_3x8_1_g, dec_3x8_1_h, not_2_out, sub_4_1_out_3;
  wire [3:0] add_4_1_out_4, buffer_6_out_3, not_1_out_2, or_2_s, rot_d_1_out_3, rot_e_1_abcd_2, sub_4_1_out_4;

  or or_1 (out_5, and_1_out, and_2_out);
  and and_1 (and_1_out, add_4_1_out_3, dec_3x8_1_b);
  and and_2 (and_2_out, sub_4_1_out_3, dec_3x8_1_c);
  Dec__3x8 dec_3x8_1 (
    .Controle(Controle), .a(dec_3x8_1_a), .b(dec_3x8_1_b), .c(dec_3x8_1_c), .d(dec_3x8_1_d), .e(dec_3x8_1_e),
    .f(dec_3x8_1_f), .g(dec_3x8_1_g), .h(dec_3x8_1_h));
  Buffer buffer_1 (.B(B), .C(dec_3x8_1_a), .out_3(S));
  ADD_4 add_4_1 (.out_3(add_4_1_out_3), .A(A), .B(B), .out_4(add_4_1_out_4));
  Buffer buffer_2 (.B(add_4_1_out_4), .C(dec_3x8_1_b), .out_3(S));
  SUB_4 sub_4_1 (.A(A), .out_3(sub_4_1_out_3), .B(B), .out_4(sub_4_1_out_4));
  and and_3 (Zero, ~S[0], ~S[1], ~S[2], ~S[3], ~dec_3x8_1_g, ~dec_3x8_1_h);  // AND_Gate
  Buffer buffer_3 (.B(sub_4_1_out_4), .C(dec_3x8_1_c), .out_3(S));
  OR or_2 (.B(A), .A(B), .S(or_2_s));
  Buffer buffer_4 (.B(or_2_s), .C(dec_3x8_1_d), .out_3(S));
  NOT not_1 (.B(B), .out_2(not_1_out_2));
  Buffer buffer_5 (.B(not_1_out_2), .C(dec_3x8_1_e), .out_3(S));
  ROT_E rot_e_1 (.ABCD_2(rot_e_1_abcd_2), .abcd(A), .XY(B[1:0]));
  ROT_D rot_d_1 (.out_3(rot_d_1_out_3), .ABCD(A), .XY(B[1:0]));
  Buffer buffer_6 (.B(rot_e_1_abcd_2), .C(not_2_out), .out_3(buffer_6_out_3));
  Buffer buffer_7 (.B(rot_d_1_out_3), .C(D), .out_3(buffer_6_out_3));
  not not_2 (not_2_out, D);
  Buffer buffer_8 (.B(buffer_6_out_3), .C(dec_3x8_1_f), .out_3(S));

  // Notes on the sheet:
  //   S: pull=up
endmodule

module ADD_1 (
  input  A,
  input  B,
  input  Vem_1,
  output S,
  output Vem_1_2
);

  wire and_1_out, and_2_out, and_3_out, and_4_out, and_5_out, and_6_out, and_7_out, not_1_out, not_2_out,
       not_3_out, not_4_out, not_5_out, not_6_out;

  not not_1 (not_1_out, A);
  not not_2 (not_2_out, B);
  not not_3 (not_3_out, A);
  not not_4 (not_4_out, Vem_1);
  not not_5 (not_5_out, B);
  not not_6 (not_6_out, Vem_1);
  and and_1 (and_1_out, B, Vem_1);
  and and_2 (and_2_out, A, Vem_1);
  and and_3 (and_3_out, A, B);
  and and_4 (and_4_out, not_1_out, not_2_out, Vem_1);
  and and_5 (and_5_out, not_3_out, B, not_4_out);
  and and_6 (and_6_out, A, not_5_out, not_6_out);
  and and_7 (and_7_out, A, B, Vem_1);
  or or_1 (Vem_1_2, and_1_out, and_2_out, and_3_out);
  ExactlyOne xor_1 (.out(S), .in0(and_4_out), .in1(and_5_out), .in2(and_6_out), .in3(and_7_out));
endmodule

module ADD_4 (
  input  [3:0] B,
  input  [3:0] A,
  output out_3,
  output [3:0] out_4
);

  wire add_1_2_vem_1_2, add_1_3_vem_1_2, add_1_4_vem_1_2;

  // Probe on A
  ADD_1 add_1_1 (.A(A[3]), .B(B[3]), .Vem_1(add_1_2_vem_1_2), .S(out_4[3]), .Vem_1_2(out_3));
  ADD_1 add_1_2 (.A(A[2]), .B(B[2]), .Vem_1(add_1_3_vem_1_2), .S(out_4[2]), .Vem_1_2(add_1_2_vem_1_2));
  ADD_1 add_1_3 (.A(A[1]), .B(B[1]), .Vem_1(add_1_4_vem_1_2), .S(out_4[1]), .Vem_1_2(add_1_3_vem_1_2));
  // Probe on out_4
  ADD_1 add_1_4 (.A(A[0]), .B(B[0]), .Vem_1(1'b0), .S(out_4[0]), .Vem_1_2(add_1_4_vem_1_2));
  // Probe on B
endmodule

module OR_4 (
  input  [3:0] B,
  input  [3:0] A,
  output [3:0] S
);

  or or_1 (S[3], A[3], B[3]);
  or or_2 (S[2], A[2], B[2]);
  or or_3 (S[1], A[1], B[1]);
  or or_4 (S[0], A[0], B[0]);
endmodule

module NOT (
  input  [3:0] B,
  output [3:0] out_2
);

  not not_1 (out_2[3], B[3]);
  not not_2 (out_2[2], B[2]);
  not not_3 (out_2[1], B[1]);
  not not_4 (out_2[0], B[0]);
endmodule

module Buffer (
  input  [3:0] B,
  input  C,
  output [3:0] out_3
);

  assign out_3[3] = C ? B[3] : 1'bz;  // Controlled_Buffer controlled_buffer_1
  assign out_3[1] = C ? B[1] : 1'bz;  // Controlled_Buffer controlled_buffer_2
  assign out_3[2] = C ? B[2] : 1'bz;  // Controlled_Buffer controlled_buffer_3
  assign out_3[0] = C ? B[0] : 1'bz;  // Controlled_Buffer controlled_buffer_4
endmodule

module Dec__3x8 (
  input  [2:0] Controle,
  output a,
  output b,
  output c,
  output d,
  output e,
  output f,
  output g,
  output h
);

  wire not_1_out, not_2_out, not_3_out, not_4_out, not_5_out, not_6_out, not_7_out, not_8_out, not_9_out,
       not_10_out, not_11_out, not_12_out;

  not not_1 (not_1_out, Controle[2]);
  not not_2 (not_2_out, Controle[1]);
  not not_3 (not_3_out, Controle[0]);
  not not_4 (not_4_out, Controle[2]);
  not not_5 (not_5_out, Controle[1]);
  not not_6 (not_6_out, Controle[2]);
  not not_7 (not_7_out, Controle[0]);
  not not_8 (not_8_out, Controle[2]);
  not not_9 (not_9_out, Controle[1]);
  not not_10 (not_10_out, Controle[0]);
  not not_11 (not_11_out, Controle[1]);
  not not_12 (not_12_out, Controle[0]);
  and and_1 (h, Controle[2], Controle[1], Controle[0]);
  and and_2 (a, not_1_out, not_2_out, not_3_out);
  and and_3 (b, not_4_out, not_5_out, Controle[0]);
  and and_4 (c, not_6_out, Controle[1], not_7_out);
  and and_5 (d, not_8_out, Controle[1], Controle[0]);
  and and_6 (e, Controle[2], not_9_out, not_10_out);
  and and_7 (f, Controle[2], not_11_out, Controle[0]);
  and and_8 (g, Controle[2], Controle[1], not_12_out);
endmodule

module OR (
  input  [3:0] B,
  input  [3:0] A,
  output [3:0] S
);

  or or_1 (S[3], A[3], B[3]);
  or or_2 (S[2], A[2], B[2]);
  or or_3 (S[1], A[1], B[1]);
  or or_4 (S[0], A[0], B[0]);
endmodule

module ROT_E (
  input  [3:0] abcd,
  input  [1:0] XY,
  output [3:0] ABCD_2
);

  wire and_1_out, and_2_out, and_3_out, and_4_out, and_5_out, and_6_out, and_7_out, and_8_out, and_9_out;

  and and_1 (and_1_out, ~XY[1], ~XY[0], abcd[3]);  // AND_Gate
  and and_2 (and_2_out, ~XY[1], XY[0], abcd[2]);  // AND_Gate
  and and_3 (and_3_out, XY[1], ~XY[0], abcd[1]);  // AND_Gate
  and and_4 (and_4_out, XY[1], XY[0], abcd[0]);
  and and_5 (and_5_out, ~XY[1], ~XY[0], abcd[2]);  // AND_Gate
  and and_6 (and_6_out, ~XY[1], XY[0], abcd[1]);  // AND_Gate
  and and_7 (and_7_out, XY[1], ~XY[0], abcd[0]);  // AND_Gate
  and and_8 (and_8_out, ~XY[1], ~XY[0], abcd[1]);  // AND_Gate
  and and_9 (and_9_out, ~XY[1], XY[0], abcd[0]);  // AND_Gate
  and and_10 (ABCD_2[0], ~XY[1], ~XY[0], abcd[0]);  // AND_Gate
  or or_1 (ABCD_2[3], and_1_out, and_2_out, and_3_out, and_4_out);
  or or_2 (ABCD_2[2], and_5_out, and_6_out, and_7_out);
  or or_3 (ABCD_2[1], and_8_out, and_9_out);
endmodule

module ROT_D (
  input  [3:0] ABCD,
  input  [1:0] XY,
  output [3:0] out_3
);

  wire and_1_out, and_2_out, and_3_out, and_4_out, and_5_out, and_6_out, and_7_out, and_8_out, and_9_out;

  and and_1 (and_1_out, ~XY[1], ~XY[0], ABCD[0]);  // AND_Gate
  and and_2 (and_2_out, ~XY[1], XY[0], ABCD[1]);  // AND_Gate
  and and_3 (and_3_out, XY[1], ~XY[0], ABCD[2]);  // AND_Gate
  and and_4 (and_4_out, XY[1], XY[0], ABCD[3]);
  and and_5 (and_5_out, ~XY[1], ~XY[0], ABCD[1]);  // AND_Gate
  and and_6 (and_6_out, ~XY[1], XY[0], ABCD[2]);  // AND_Gate
  and and_7 (and_7_out, XY[1], ~XY[0], ABCD[3]);  // AND_Gate
  and and_8 (and_8_out, ~XY[1], ~XY[0], ABCD[2]);  // AND_Gate
  and and_9 (and_9_out, ~XY[1], XY[0], ABCD[3]);  // AND_Gate
  and and_10 (out_3[3], ~XY[1], ~XY[0], ABCD[3]);  // AND_Gate
  or or_1 (out_3[0], and_1_out, and_2_out, and_3_out, and_4_out);
  or or_2 (out_3[1], and_5_out, and_6_out, and_7_out);
  or or_3 (out_3[2], and_8_out, and_9_out);
endmodule

// A
module SUB_4 (
  input  [3:0] B,
  input  [3:0] A,
  output out_3,
  output [3:0] out_4
);

  wire sub_1_2_vai_1, sub_1_3_vai_1, sub_1_4_vai_1;

  // Probe on A
  SUB_1 sub_1_1 (.A(A[3]), .B(B[3]), .VEM_1(sub_1_2_vai_1), .S(out_4[3]), .VAI_1(out_3));
  SUB_1 sub_1_2 (.A(A[2]), .B(B[2]), .VEM_1(sub_1_3_vai_1), .S(out_4[2]), .VAI_1(sub_1_2_vai_1));
  SUB_1 sub_1_3 (.A(A[1]), .B(B[1]), .VEM_1(sub_1_4_vai_1), .S(out_4[1]), .VAI_1(sub_1_3_vai_1));
  // Probe on out_4
  SUB_1 sub_1_4 (.A(A[0]), .B(B[0]), .VEM_1(1'b0), .S(out_4[0]), .VAI_1(sub_1_4_vai_1));
  // Probe on B
endmodule

module SUB_1 (
  input  A,
  input  B,
  input  VEM_1,
  output S,
  output VAI_1
);

  wire and_1_out, and_2_out, and_3_out, and_4_out, and_5_out, and_6_out, and_7_out, not_1_out, not_2_out,
       not_3_out, not_4_out, not_5_out, not_6_out, not_7_out, not_8_out;

  not not_1 (not_1_out, A);
  not not_2 (not_2_out, B);
  not not_3 (not_3_out, A);
  not not_4 (not_4_out, VEM_1);
  not not_5 (not_5_out, B);
  not not_6 (not_6_out, VEM_1);
  not not_7 (not_7_out, A);
  not not_8 (not_8_out, A);
  and and_1 (and_1_out, not_1_out, not_2_out, VEM_1);
  and and_2 (and_2_out, not_3_out, B, not_4_out);
  and and_3 (and_3_out, A, not_5_out, not_6_out);
  and and_4 (and_4_out, A, B, VEM_1);
  and and_5 (and_5_out, not_7_out, VEM_1);
  and and_6 (and_6_out, not_8_out, B);
  and and_7 (and_7_out, B, VEM_1);
  or or_1 (S, and_1_out, and_2_out, and_3_out, and_4_out);
  or or_2 (VAI_1, and_5_out, and_6_out, and_7_out);
endmodule

module Mux (
  input  [3:0] A,
  input  [3:0] b,
  input  Controle,
  output [3:0] S
);

  wire not_1_out;

  Buffer buffer_1 (.B(A), .C(not_1_out), .out_3(S));
  not not_1 (not_1_out, Controle);
  Buffer buffer_2 (.B(b), .C(Controle), .out_3(S));
endmodule

module AC (
  input  in_1,
  input  [3:0] D,
  output [3:0] Q
);

  D_Flip_Flop d_ff_1 (.clk(in_1), .D(D[3]), .Q(Q[3]));  // open: Qn, preset, en, reset
  D_Flip_Flop d_ff_2 (.clk(in_1), .D(D[2]), .Q(Q[2]));  // open: Qn, preset, en, reset
  D_Flip_Flop d_ff_3 (.clk(in_1), .D(D[1]), .Q(Q[1]));  // open: Qn, preset, en, reset
  D_Flip_Flop d_ff_4 (.clk(in_1), .D(D[0]), .Q(Q[0]));  // open: Qn, preset, en, reset
endmodule

module IR (
  input  Clock,
  input  [7:0] E,
  output [7:0] Q
);

  D_Flip_Flop D7 (.clk(Clock), .D(E[7]), .Q(Q[7]));  // open: Qn, preset, en, reset
  D_Flip_Flop D6 (.clk(Clock), .D(E[6]), .Q(Q[6]));  // open: Qn, preset, en, reset
  D_Flip_Flop D5 (.clk(Clock), .D(E[5]), .Q(Q[5]));  // open: Qn, preset, en, reset
  D_Flip_Flop D4 (.clk(Clock), .D(E[4]), .Q(Q[4]));  // open: Qn, preset, en, reset
  D_Flip_Flop D3 (.clk(Clock), .D(E[3]), .Q(Q[3]));  // open: Qn, preset, en, reset
  D_Flip_Flop D2 (.clk(Clock), .D(E[2]), .Q(Q[2]));  // open: Qn, preset, en, reset
  D_Flip_Flop D0 (.clk(Clock), .D(E[0]), .Q(Q[0]));  // open: Qn, preset, en, reset
  D_Flip_Flop D1 (.clk(Clock), .D(E[1]), .Q(Q[1]));  // open: Qn, preset, en, reset
endmodule

// INSTRUÇÃO
module UC (
  input  [7:0] in_1,
  output [3:0] OPERANDO,
  output E,
  output [2:0] OPCODE
);


  assign E = in_1[4];
  assign OPCODE = in_1[7:5];
  assign OPERANDO = in_1[3:0];
endmodule
