// Logisim project TESTE.circ45.circ as structural Verilog: 7 circuits, main circuit main
module main (
  input  [3:0] B,
  input  [3:0] A,
  input  [2:0] Controle,
  output out_4,
  output [3:0] out_5
);

  wire dec_3x8_1_a, dec_3x8_1_b, dec_3x8_1_c, dec_3x8_1_d;
  wire [3:0] add_4_1_out_4, not_1_out_2, or_1_s;

  Dec__3x8 dec_3x8_1 (
    .Corrente(Controle), .a(dec_3x8_1_a), .b(dec_3x8_1_b), .c(dec_3x8_1_c), .d(dec_3x8_1_d));  // open: e, f, g, h
  Buffer buffer_1 (.B(B), .C(dec_3x8_1_a), .out_3(out_5));
  ADD_4 add_4_1 (.out_3(out_4), .in_2(A), .in_1(B), .out_4(add_4_1_out_4));
  Buffer buffer_2 (.B(add_4_1_out_4), .C(dec_3x8_1_b), .out_3(out_5));
  OR or_1 (.B(A), .A(B), .S(or_1_s));
  Buffer buffer_3 (.B(or_1_s), .C(dec_3x8_1_c), .out_3(out_5));
  NOT not_1 (.B(B), .out_2(not_1_out_2));
  Buffer buffer_4 (.B(not_1_out_2), .C(dec_3x8_1_d), .out_3(out_5));
endmodule

module ADD_1 (
  input  in_1,
  input  in_2,
  input  in_3,
  output out_4,
  output out_5
);

  wire and_1_out, and_2_out, and_3_out, and_4_out, and_5_out, and_6_out, and_7_out, not_1_out, not_2_out,
       not_3_out, not_4_out, not_5_out, not_6_out;

  not not_1 (not_1_out, in_1);
  not not_2 (not_2_out, in_2);
  not not_3 (not_3_out, in_1);
  not not_4 (not_4_out, in_3);
  not not_5 (not_5_out, in_2);
  not not_6 (not_6_out, in_3);
  and and_1 (and_1_out, in_2, in_3);
  and and_2 (and_2_out, in_1, in_3);
  and and_3 (and_3_out, in_1, in_2);
  and and_4 (and_4_out, not_1_out, not_2_out, in_3);
  and and_5 (and_5_out, not_3_out, in_2, not_4_out);
  and and_6 (and_6_out, in_1, not_5_out, not_6_out);
  and and_7 (and_7_out, in_1, in_2, in_3);
  or or_1 (out_5, and_1_out, and_2_out, and_3_out);
  ExactlyOne xor_1 (.out(out_4), .in0(and_4_out), .in1(and_5_out), .in2(and_6_out), .in3(and_7_out));
endmodule

module ADD_4 (
  input  [3:0] in_1,
  input  [3:0] in_2,
  output out_3,
  output [3:0] out_4
);

  wire add_1_2_out_5, add_1_3_out_5, add_1_4_out_5;

  // Probe on in_2
  ADD_1 add_1_1 (.in_1(in_2[3]), .in_2(in_1[3]), .in_3(add_1_2_out_5), .out_4(out_4[3]), .out_5(out_3));
  ADD_1 add_1_2 (.in_1(in_2[2]), .in_2(in_1[2]), .in_3(add_1_3_out_5), .out_4(out_4[2]), .out_5(add_1_2_out_5));
  ADD_1 add_1_3 (.in_1(in_2[1]), .in_2(in_1[1]), .in_3(add_1_4_out_5), .out_4(out_4[1]), .out_5(add_1_3_out_5));
  // Probe on out_4
  ADD_1 add_1_4 (.in_1(in_2[0]), .in_2(in_1[0]), .in_3(1'b0), .out_4(out_4[0]), .out_5(add_1_4_out_5));
  // Probe on in_1
endmodule

module Dec__3x8 (
  input  [2:0] Corrente,
  output a,
  output b,
  output c,
  output d,
  output e,
  output f,
  output g,
  output h
);

  wire not_1_out, not_2_out, not_3_out, not_4_out, not_5_out, not_6_out, not_7_out, not_8_out, not_9_out,
       not_10_out, not_11_out, not_12_out;

  not not_1 (not_1_out, Corrente[2]);
  not not_2 (not_2_out, Corrente[1]);
  not not_3 (not_3_out, Corrente[0]);
  not not_4 (not_4_out, Corrente[2]);
  not not_5 (not_5_out, Corrente[1]);
  not not_6 (not_6_out, Corrente[2]);
  not not_7 (not_7_out, Corrente[0]);
  not not_8 (not_8_out, Corrente[2]);
  not not_9 (not_9_out, Corrente[1]);
  not not_10 (not_10_out, Corrente[0]);
  not not_11 (not_11_out, Corrente[1]);
  not not_12 (not_12_out, Corrente[0]);
  and and_1 (h, Corrente[2], Corrente[1], Corrente[0]);
  and and_2 (a, not_1_out, not_2_out, not_3_out);
  and and_3 (b, not_4_out, not_5_out, Corrente[0]);
  and and_4 (c, not_6_out, Corrente[1], not_7_out);
  and and_5 (d, not_8_out, Corrente[1], Corrente[0]);
  and and_6 (e, Corrente[2], not_9_out, not_10_out);
  and and_7 (f, Corrente[2], not_11_out, Corrente[0]);
  and and_8 (g, Corrente[2], Corrente[1], not_12_out);
endmodule

module OR (
  input  [3:0] B,
  input  [3:0] A,
  output [3:0] S
);

  or or_1 (S[3], A[3], B[3]);
  or or_2 (S[2], A[2], B[2]);
  or or_3 (S[1], A[1], B[1]);
  or or_4 (S[0], A[0], B[0]);
endmodule

module NOT (
  input  [3:0] B,
  output [3:0] out_2
);

  not not_1 (out_2[3], B[3]);
  not not_2 (out_2[1], B[1]);
  not not_3 (out_2[2], B[2]);
  not not_4 (out_2[0], B[0]);
endmodule

module Buffer (
  input  [3:0] B,
  input  C,
  output [3:0] out_3
);

  assign out_3[1] = C ? B[1] : 1'bz;  // Controlled_Buffer controlled_buffer_1
  assign out_3[3] = C ? B[3] : 1'bz;  // Controlled_Buffer controlled_buffer_2
  assign out_3[2] = C ? B[2] : 1'bz;  // Controlled_Buffer controlled_buffer_3
  assign out_3[0] = C ? B[0] : 1'bz;  // Controlled_Buffer controlled_buffer_4
endmodule
